// Logisim project Binary to Decimal Converter.circ as structural Verilog: 2 circuits, main circuit main
module Input_Register (
  input  Shift,
  input  in_2,
  input  in_3,
  input  in_4,
  input  in_5,
  input  in_6,
  input  in_7,
  input  in_8,
  input  in_9,
  input  in_10,
  input  in_11,
  input  in_12,
  input  in_13,
  input  in_14,
  input  in_15,
  input  in_16,
  input  in_17,
  input  Carry_In,
  input  Clear,
  input  Clock,
  input  Enable,
  output Carry_Out
);

  wire nand_1_out, nand_2_out, nand_3_out, nand_4_out, nand_5_out, nand_6_out, nand_7_out, nand_8_out,
       nand_9_out, nand_10_out, nand_11_out, nand_12_out, nand_13_out, nand_14_out, nand_15_out, nand_16_out,
       nand_17_out, nand_18_out, nand_19_out, nand_20_out, nand_21_out, nand_22_out, nand_23_out,
       nand_24_out, nand_25_out, nand_26_out, nand_27_out, nand_28_out, nand_29_out, nand_30_out,
       nand_31_out, nand_32_out, nand_33_out, nand_34_out, nand_35_out, nand_36_out, nand_37_out,
       nand_38_out, nand_39_out, nand_40_out, nand_41_out, nand_42_out, nand_43_out, nand_44_out,
       nand_45_out, nand_46_out, nand_47_out, nand_48_out, not_1_out, register_2_q, register_3_q,
       register_4_q, register_5_q, register_6_q, register_7_q, register_8_q, register_9_q, register_10_q,
       register_11_q, register_12_q, register_13_q, register_14_q, register_15_q, register_16_q;

  not not_1 (not_1_out, Shift);
  nand nand_1 (nand_1_out, register_2_q, Shift);
  nand nand_2 (nand_2_out, not_1_out, in_2);
  nand nand_3 (nand_3_out, nand_1_out, nand_2_out);
  Register #(.width(1)) register_1 (.D(nand_3_out), .en(Enable), .Q(Carry_Out), .clk(Clock), .clr(Clear));
  nand nand_4 (nand_4_out, register_3_q, Shift);
  nand nand_5 (nand_5_out, not_1_out, in_3);
  nand nand_6 (nand_6_out, nand_4_out, nand_5_out);
  nand nand_7 (nand_7_out, register_4_q, Shift);
  nand nand_8 (nand_8_out, not_1_out, in_4);
  nand nand_9 (nand_9_out, nand_7_out, nand_8_out);
  Register #(.width(1)) register_2 (.D(nand_6_out), .en(Enable), .Q(register_2_q), .clk(Clock), .clr(Clear));
  nand nand_10 (nand_10_out, register_5_q, Shift);
  nand nand_11 (nand_11_out, nand_10_out, nand_12_out);
  Register #(.width(1)) register_3 (.D(nand_9_out), .en(Enable), .Q(register_3_q), .clk(Clock), .clr(Clear));
  nand nand_12 (nand_12_out, not_1_out, in_5);
  nand nand_13 (nand_13_out, register_6_q, Shift);
  nand nand_14 (nand_14_out, nand_13_out, nand_15_out);
  Register #(.width(1)) register_4 (.D(nand_11_out), .en(Enable), .Q(register_4_q), .clk(Clock), .clr(Clear));
  nand nand_15 (nand_15_out, not_1_out, in_6);
  nand nand_16 (nand_16_out, register_7_q, Shift);
  Register #(.width(1)) register_5 (.D(nand_14_out), .en(Enable), .Q(register_5_q), .clk(Clock), .clr(Clear));
  nand nand_17 (nand_17_out, not_1_out, in_7);
  nand nand_18 (nand_18_out, register_8_q, Shift);
  nand nand_19 (nand_19_out, nand_16_out, nand_17_out);
  Register #(.width(1)) register_6 (.D(nand_19_out), .en(Enable), .Q(register_6_q), .clk(Clock), .clr(Clear));
  nand nand_20 (nand_20_out, not_1_out, in_8);
  nand nand_21 (nand_21_out, nand_18_out, nand_20_out);
  Register #(.width(1)) register_7 (.D(nand_21_out), .en(Enable), .Q(register_7_q), .clk(Clock), .clr(Clear));
  nand nand_22 (nand_22_out, register_9_q, Shift);
  nand nand_23 (nand_23_out, not_1_out, in_9);
  nand nand_24 (nand_24_out, nand_22_out, nand_23_out);
  Register #(.width(1)) register_8 (.D(nand_24_out), .en(Enable), .Q(register_8_q), .clk(Clock), .clr(Clear));
  nand nand_25 (nand_25_out, register_10_q, Shift);
  nand nand_26 (nand_26_out, not_1_out, in_10);
  nand nand_27 (nand_27_out, nand_25_out, nand_26_out);
  Register #(.width(1)) register_9 (.D(nand_27_out), .en(Enable), .Q(register_9_q), .clk(Clock), .clr(Clear));
  nand nand_28 (nand_28_out, not_1_out, in_11);
  nand nand_29 (nand_29_out, register_11_q, Shift);
  nand nand_30 (nand_30_out, nand_29_out, nand_28_out);
  nand nand_31 (nand_31_out, register_12_q, Shift);
  nand nand_32 (nand_32_out, not_1_out, in_12);
  nand nand_33 (nand_33_out, nand_31_out, nand_32_out);
  Register #(.width(1)) register_10 (.D(nand_30_out), .en(Enable), .Q(register_10_q), .clk(Clock), .clr(Clear));
  nand nand_34 (nand_34_out, register_13_q, Shift);
  nand nand_35 (nand_35_out, nand_34_out, nand_36_out);
  Register #(.width(1)) register_11 (.D(nand_33_out), .en(Enable), .Q(register_11_q), .clk(Clock), .clr(Clear));
  nand nand_36 (nand_36_out, not_1_out, in_13);
  nand nand_37 (nand_37_out, register_14_q, Shift);
  nand nand_38 (nand_38_out, nand_37_out, nand_39_out);
  Register #(.width(1)) register_12 (.D(nand_35_out), .en(Enable), .Q(register_12_q), .clk(Clock), .clr(Clear));
  nand nand_39 (nand_39_out, not_1_out, in_14);
  nand nand_40 (nand_40_out, register_15_q, Shift);
  Register #(.width(1)) register_13 (.D(nand_38_out), .en(Enable), .Q(register_13_q), .clk(Clock), .clr(Clear));
  nand nand_41 (nand_41_out, not_1_out, in_15);
  nand nand_42 (nand_42_out, register_16_q, Shift);
  nand nand_43 (nand_43_out, nand_40_out, nand_41_out);
  Register #(.width(1)) register_14 (.D(nand_43_out), .en(Enable), .Q(register_14_q), .clk(Clock), .clr(Clear));
  nand nand_44 (nand_44_out, not_1_out, in_16);
  nand nand_45 (nand_45_out, nand_42_out, nand_44_out);
  Register #(.width(1)) register_15 (.D(nand_45_out), .en(Enable), .Q(register_15_q), .clk(Clock), .clr(Clear));
  nand nand_46 (nand_46_out, Carry_In, Shift);
  nand nand_47 (nand_47_out, not_1_out, in_17);
  nand nand_48 (nand_48_out, nand_46_out, nand_47_out);
  Register #(.width(1)) register_16 (.D(nand_48_out), .en(Enable), .Q(register_16_q), .clk(Clock), .clr(Clear));
endmodule

module Digit_Register (
  input  Carry_In,
  input  Clock,
  input  Clear,
  input  EN,
  output Carry_Out,
  output [3:0] BCD_Output
);

  wire and_1_out, and_2_out, and_3_out, nand_1_out, nand_2_out, nand_3_out, nand_4_out, or_2_out, or_3_out,
       xor_1_out, xor_2_out, xor_3_out, xor_4_out;

  or or_1 (Carry_Out, and_1_out, BCD_Output[3]);
  and and_1 (and_1_out, nand_3_out, BCD_Output[2]);
  Register #(.width(1)) register_1 (.D(xor_1_out), .en(EN), .Q(BCD_Output[3]), .clk(Clock), .clr(Clear));
  or or_2 (or_2_out, BCD_Output[0], BCD_Output[1]);
  and and_2 (and_2_out, or_2_out, BCD_Output[2]);
  or or_3 (or_3_out, BCD_Output[3], and_2_out);
  xor xor_1 (xor_1_out, nand_3_out, BCD_Output[2]);
  Register #(.width(1)) register_2 (.D(xor_3_out), .en(EN), .Q(BCD_Output[2]), .clk(Clock), .clr(Clear));
  nand nand_1 (nand_1_out, or_3_out, and_3_out);
  nand nand_2 (nand_2_out, and_3_out, BCD_Output[1]);
  nand nand_3 (nand_3_out, nand_1_out, nand_2_out, nand_4_out);
  nand nand_4 (nand_4_out, or_3_out, BCD_Output[1]);
  xor xor_2 (xor_2_out, or_3_out, BCD_Output[1]);
  xor xor_3 (xor_3_out, and_3_out, xor_2_out);
  Register #(.width(1)) register_3 (.D(xor_4_out), .en(EN), .Q(BCD_Output[1]), .clk(Clock), .clr(Clear));
  and and_3 (and_3_out, or_3_out, BCD_Output[0]);
  xor xor_4 (xor_4_out, or_3_out, BCD_Output[0]);
  Register #(.width(1)) register_4 (.D(Carry_In), .en(EN), .Q(BCD_Output[0]), .clk(Clock), .clr(Clear));

  // Notes on the sheet:
  //   Greater than 4?
  //   Add 3, then shift.
  //   Store Results
endmodule
